// Logisim project design.circ as structural Verilog: 1 circuit, main circuit main
module main (
);

  wire _1_out, _4_out, AC_out;
  wire [6:0] register_1_q;

  Register #(.width(7)) register_1 (.Q(register_1_q), .clk(_4_out));  // open: D, en, clr
  Register #(.width(7)) register_2 (.clk(_1_out));  // open: D, en, Q, clr
  TTY #(.rows(1), .cols(30)) tty_1 (.data(register_1_q), .clk(_4_out), .clr(AC_out));  // open: we
  Button _1 (.out(_1_out));
  Button _2 ();  // open: out
  Button _5 ();  // open: out
  Button _4 (.out(_4_out));
  Button _8 ();  // open: out
  Button _8_2 ();  // open: out
  Button _0 ();  // open: out
  Button AC (.out(AC_out));
  Button _3 ();  // open: out
  Button _7 ();  // open: out
  Button _9 ();  // open: out
  Button button ();  // open: out
  Button button_2 ();  // open: out
  Button button_3 ();  // open: out
  Button button_4 ();  // open: out
  Button button_5 ();  // open: out
  Button button_6 ();  // open: out
  Button x ();  // open: out
  Button x_y ();  // open: out
  Button button_7 ();  // open: out
endmodule
